# Fritzing sketch pico-ds3502 (saved by Fritzing 1.0.5)
breadboards: 1

parts:
  Part1 = Adafruit DS3502
  Mod1 = Raspberry Pi Pico

nets:
  N1: Part1.RL, Part1.GND, Mod1.pin_3, Mod1.pin_8, Mod1.pin_13, Mod1.pin_18, Mod1.pin_23, Mod1.pin_28, Mod1.pin_33, Mod1.pin_38
  N2: Part1.RW, Mod1.pin_31
  N3: Part1.RH, Part1.VCC, Mod1.pin_36
  N4: Part1.SCL, Mod1.pin_22
  N5: Part1.SDA, Mod1.pin_21

custom parts:
  Raspberry Pi Pico: Raspberry Pi Pico. Based around the RP2040 microcontroller the Pico is a low cost microcontroller device bringing Raspberry Pi quality, cost, and easy of use to the microcontroller space. Jan 2021, Split part in to two versions: tht (this one) and SMD. This one will drill holes for a .1 in header in pcb to allow plugging in the module as well as providing pads to solder the module to the top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
